// Digital circuit ALU-visual.dig as structural Verilog
module ALU_visual (
  input  [7:0] A,
  input  [7:0] B,
  input  [3:0] S,
  output [7:0] R
);

  wire div, left, load, multi, \nand , right, soma, sub, \xor ;

  ALU_8bit alu_8bit_1 (
    .Soma(soma), .Sub(sub), .Multi(multi), .Div(div), .NAND(\nand ), .XOR(\xor ), .Right(right), .Left(left),
    .A(A), .B(B), .Load(load), .S(R));
  Seletor seletor_1 (
    .S(S), .Load(load), .Soma(soma), .Sub(sub), .Multi(multi), .Div(div), .Right(right), .Left(left),
    .NAND(\nand ), .XOR(\xor ));
endmodule
